# Fritzing sketch pcb (saved by Fritzing 0.9.3b)
circuit board: 5.66067cm x 5.21661cm
breadboards: 1

parts:
  J17 = female pin header, 4 pins [form="♀ (female)"]
  J18 = female pin header, 1 pin [form="♀ (female)"]
  J19 = female pin header, 1 pin [form="♀ (female)"]
  J20 = female pin header, 1 pin [form="♀ (female)"]
  J21 = female pin header, 1 pin [form="♀ (female)"]
  J22 = double row female pin header, 8 pins [form="♀ (female)"]
  J25 = female pin header, 1 pin [form="♀ (female)"]
  J26 = female pin header, 1 pin [form="♀ (female)"]
  J27 = female pin header, 1 pin [form="♀ (female)"]
  J28 = female pin header, 1 pin [form="♀ (female)"]
  J24 = female pin header, 2 pins [form="♀ (female)"]
  J23 = female pin header, 2 pins [form="♀ (female)"]
  J30 = female pin header, 2 pins [form="♀ (female)"]
  J31 = female pin header, 2 pins [form="♀ (female)"]
  R1 = Resistor [tolerance=±5% resistance=220 package=THT]
  IC1 = IC, DIP package, 14 pins [chip_label=IC]
  J33 = female pin header, 1 pin [form="♀ (female)"]
  J40 = female pin header, 1 pin [form="♀ (female)"]
  Componente2 = Arduino Uno (Rev3)
  J47 = female pin header, 1 pin [form="♀ (female)"]
  J48 = female pin header, 1 pin [form="♀ (female)"]
  J49 = female pin header, 1 pin [form="♀ (female)"]
  J50 = female pin header, 1 pin [form="♀ (female)"]

nets:
  N1: J17.pin1, J24.pin1, IC1.pin4, Componente2.5V
  N2: J17.pin2, J23.pin2, Componente2.A5/SCL
  N3: J17.pin3, J17.pin4, J19.pin1, J22.pin4, J24.pin2, J31.pin2, R1.Pin_0, J40.pin1, Componente2.GND, J48.pin1
  N4: J18.pin1, IC1.pin3
  N5: J20.pin1, IC1.pin11, J49.pin1, J50.pin1
  N6: J21.pin1, IC1.pin12
  N7: J22.pin1, J27.pin1
  N8: J22.pin5, Componente2.D3_PWM
  N9: J22.pin7, J22.pin8, J25.pin1
  N10: J26.pin1, Componente2.3V3
  N11: J28.pin1, Componente2.D2
  N12: J23.pin1, IC1.pin13, IC1.pin14, Componente2.A4/SDA
  N13: J30.pin1, Componente2.D7
  N14: J30.pin2, R1.Pin_1
  N15: J31.pin1, Componente2.VIN
  N16: IC1.pin1, IC1.pin2, Componente2.A0
  N17: IC1.pin5, J47.pin1
  N18: IC1.pin6, IC1.pin7, Componente2.A2
  N19: IC1.pin8, IC1.pin9, Componente2.A3
  N20: IC1.pin10, J33.pin1
